// Logisim project my log.circ as structural Verilog: 1 circuit, main circuit main
module main (
  input  in_1,
  input  [1:0] set__01,
  input  in_3,
  input  in_4,
  input  set_Q___1___0,
  input  in_6,
  input  [1:0] set__11,
  input  in_8,
  input  [1:0] set__01_2,
  input  in_10,
  input  [2:0] in_11,
  input  set__100,
  input  [2:0] set__000,
  output [3:0] out_14,
  output [3:0] out_15,
  output [3:0] out_16,
  output [3:0] out_17
);

  wire clock_1_out, comparator_1_eq, not_1_out, Q_1_q;
  wire [1:0] adder_2_out, bit_extender_1_out, bit_extender_2_out, shifter_2_out;
  wire [2:0] counter_1_q;
  wire [3:0] A_q, adder_1_out, adder_3_out, bit_extender_3_out, M_q, Q_q, shifter_1_out, shifter_4_out,
       subtractor_1_out;

  Clock clock_1 (.out(clock_1_out));
  Register #(.width(4)) M (.en(in_1), .Q(M_q), .clk(clock_1_out));  // open: D, clr
  Register #(.width(4)) A (.D(out_16), .en(in_4), .Q(A_q), .clk(clock_1_out));  // open: clr
  Register #(.width(4)) Q (.D(out_17), .en(in_6), .Q(Q_q), .clk(clock_1_out));  // open: clr
  Shifter #(.width(4), .shift("lr")) shifter_1 (.in(Q_q), .\dist (set__01_2), .out(shifter_1_out));
  assign bit_extender_1_out = {{1{1'b0}}, Q_q[0]};  // Bit_Extender bit_extender_1
  Register #(.width(1)) Q_1 (.D(Q_q[0]), .en(in_8), .Q(Q_1_q), .clk(clock_1_out));  // open: clr
  Adder #(.width(4)) adder_1 (.a(M_q), .b(A_q), .out(adder_1_out));  // open: cin, cout
  Subtractor #(.width(4)) subtractor_1 (.a(A_q), .b(M_q), .out(subtractor_1_out));  // open: bin, bout
  assign bit_extender_2_out = {{1{1'b0}}, Q_1_q};  // Bit_Extender bit_extender_2
  Counter #(.width(3), .max('h7)) counter_1 (
    .load(in_10), .D(in_11), .count(set__100), .Q(counter_1_q), .clk(clock_1_out));  // open: carry, clr
  Shifter #(.width(2)) shifter_2 (.in(bit_extender_1_out), .\dist (set_Q___1___0), .out(shifter_2_out));
  Multiplexer #(.select(2), .width(4)) multiplexer_1 (
    .in0(A_q), .in1(adder_1_out), .in2(subtractor_1_out), .in3(A_q), .out(out_14), .sel(adder_2_out),
    .en(in_3));
  Adder #(.width(2)) adder_2 (.a(shifter_2_out), .b(bit_extender_2_out), .out(adder_2_out));  // open: cin, cout
  Comparator #(.width(3)) comparator_1 (.a(counter_1_q), .b(set__000), .eq(comparator_1_eq));  // open: gt, lt
  not not_1 (not_1_out, comparator_1_eq);
  Shifter #(.width(4), .shift("lr")) shifter_3 (.in(out_14), .\dist (set__01), .out(out_15));
  assign out_16 = not_1_out ? out_15 : 4'bz;  // Controlled_Buffer controlled_buffer_1
  assign out_17 = not_1_out ? adder_3_out : 4'bz;  // Controlled_Buffer controlled_buffer_2
  assign bit_extender_3_out = {{3{1'b0}}, out_14[0]};  // Bit_Extender bit_extender_3
  Shifter #(.width(4)) shifter_4 (.in(bit_extender_3_out), .\dist (set__11), .out(shifter_4_out));
  Adder #(.width(4)) adder_3 (.a(shifter_4_out), .b(shifter_1_out), .out(adder_3_out));  // open: cin, cout

  // Notes on the sheet:
  //   set A = 0
  //   00 = A
  //   01 = A+M
  //   10 = A - M
  //   set 4
  //   11 = A
endmodule
